# Fritzing sketch schematic (saved by Fritzing 0.8.5b)
breadboards: 1

parts:
  Raspberry_Pi1 = Raspberry Pi B+
  R1 = Resistor [tolerance=±5% resistance=220 package=THT]
  LED1 = smd LED [color="Red (633nm)" package="0603 [SMD]"]

nets:
  N1: Raspberry_Pi1.GND, R1.Pin_0
  N2: Raspberry_Pi1.GIPO18, LED1.anode
  N3: R1.Pin_1, LED1.cathode

custom parts:
  Raspberry Pi B+: The awesome Raspberry Pi ARM Board with 40 pin gipo. Ready for special designed Raspberry Pi B+ Hat (Hardware attached (on) top)
